# Fritzing sketch conexion_capturaconboton (saved by Fritzing 1.0.5)
breadboards: 1

parts:
  M1 = Portenta-h7
  S1 = Pushbutton [package="[THT]"]

nets:
  N1: M1.14_TX, S1.Pin_3, S1.Pin_4
  N2: M1.GND-24, S1.Pin_1, S1.Pin_2

custom parts:
  Portenta-h7: arduino Portenta H7 ST STM32H747XI processor Dual core Cortex M7 2M flash 1M ram. Note this part does not include the 2 high density connectors, only the 28 breadboard connectors!
