# Fritzing sketch conexion_sistema (saved by Fritzing 1.0.5)
breadboards: 1

parts:
  M1 = Portenta-h7
  HLK-PM1 = HLK-PM12 [part_number=HLK-PM12]
  HLK-PM2 = HLK-PM01
  Componente1 = RFID 125Khz W26

nets:
  N1: M1.14_TX, Componente1.white
  N2: M1.RESET, Componente1.green
  N3: M1.GND-24, M1.-VBAT, HLK-PM1.-Vo, HLK-PM2.-Vo, Componente1.black
  N4: M1.5V, HLK-PM2.+Vo
  N5: HLK-PM1.+Vo, Componente1.red

custom parts:
  Portenta-h7: arduino Portenta H7 ST STM32H747XI processor Dual core Cortex M7 2M flash 1M ram. Note this part does not include the 2 high density connectors, only the 28 breadboard connectors!
  RFID 125Khz W26: RFID IP65 125Khz / W26
